# Fritzing sketch nymphiSchematic (saved by Fritzing 0.9.1b)
circuit board: 6cm x 6cm
breadboards: 1

parts:
  Composant1 = Arduino Yun
  R1 = Resistor [tolerance=±5% resistance=10k package=THT]
  R4 = Resistor [tolerance=±5% resistance=10k package=THT]
  SPKR1 = Loudspeaker
  JP3 = Header 2 [package=jst-2-pth]
  JP4 = Header 2 [package=jst-2-pth]
  JP6 = Header 4 [package=jst-4-pth]
  JP5 = Header 3 [package=jst-3-pth]
  R5 = Resistor [tolerance=±5% resistance=10k package=THT]
  R6 = Resistor [tolerance=±5% resistance=150 package=THT]
  R7 = Resistor [tolerance=±5% resistance=150 package=THT]

nets (from the schematic view):
  N1: Composant1.A0, R1.Pin_0, JP4.2
  N2: Composant1.A1, R4.Pin_0, JP3.2
  N3: Composant1.5V, JP3.1, JP4.1, JP5.1
  N4: Composant1.ICSP_MOSI, Composant1.D11_PWM/MOSI, R7.Pin_1
  N5: Composant1.D8, SPKR1.pin1
  N6: Composant1.D9_PWM, R5.Pin_1
  N7: Composant1.D10_PWM/SS, R6.Pin_1
  N8: Composant1.GND, R1.Pin_1, R4.Pin_1, SPKR1.pin2, JP6.2, JP5.3
  N9: Composant1.D7, JP5.2
  N10: JP6.1, R7.Pin_0
  N11: JP6.3, R6.Pin_0
  N12: JP6.4, R5.Pin_0

notes:
  clou 1
  clou 2
  Jp5 = dht11
  Jp6 = led RGB
  Jp4 = photocell
  Jp3 = crocodiles
